# Fritzing sketch ESP01_NowSender (saved by Fritzing 0.9.9b)
breadboards: 1

parts:
  U1 = ESP8266 ESP-01 Upgraded WiFi Module [part_number=ESP8266]
  R1 = Resistor [tolerance=±5% power=0.25 resistance=10k package=THT]
  S1 = Momentary Switch [package=ksa_sealed_tac_switch]
  DHT1 = DHT22 Humidity and Temperature Sensor
  R2 = Resistor [tolerance=±5% power=0.25 resistance=10k package=THT]
  VCC1 = Battery block 9V
  M2 = RioRand LM2596

nets:
  VCC: U1.VCC, R1.Pin_0, DHT1.VDD, R2.Pin_0, M2.Pin_3
  N1: U1.GPIO_0, DHT1.DATA, R2.Pin_1
  N2: U1.RST/GPIO_16, R1.Pin_1, S1.3
  GND: U1.GND, S1.1, DHT1.GND, M2.Pin_4
  N3: VCC1.-, M2.Pin_2
  N4: VCC1.+, M2.Pin_1

custom parts:
  ESP8266 ESP-01 Upgraded WiFi Module: Upgraded Version ESP-01,all Flash are upgraded to 1M byte.Also support Cloud service remote transmission.
